// Logisim project Data Memory.circ as structural Verilog: 1 circuit, main circuit main
module main (
  input  MemRead,
  input  MemWrite,
  input  [7:0] Address,
  input  [7:0] Write_Data,
  input  CLK,
  input  CLR,
  output [7:0] Data_Read
);

  wire not_1_out;

  not not_1 (not_1_out, CLK);
  RAM #(.bus("separate")) ram_1 (
    .addr(Address), .din(Write_Data), .data(Data_Read), .str(MemWrite), .clk(not_1_out), .ld(MemRead),
    .clr(CLR));  // open: sel
endmodule
