// Logisim project Instruction_mem.circ as structural Verilog: 1 circuit, main circuit main
module main (
  input  [7:0] PC_Write,
  input  Clock,
  input  Reset,
  output [7:0] PC_Read,
  output [3:0] Opcode,
  output [3:0] Src_1,
  output [3:0] Src_2,
  output [3:0] Dst_reg,
  output [3:0] Shft_amnt,
  output [7:0] JmpAddr,
  output [7:0] Addrss_imm
);

  wire not_1_out;

  not not_1 (not_1_out, Clock);
  Register register_1 (.Input(PC_Write), .Reset(Reset), .CLK(not_1_out), .Stored_Data(PC_Read));
  ROM #(.dataWidth(20)) rom_1 (.addr(PC_Read), .data({Opcode, JmpAddr, Addrss_imm}), .sel(1'b1));

  assign Dst_reg = Addrss_imm[7:4];
  assign Shft_amnt = Addrss_imm[3:0];
  assign Src_1 = JmpAddr[7:4];
  assign Src_2 = JmpAddr[3:0];

  // Notes on the sheet:
  //   contents of rom_1 (hex, n*v repeats v):
  //   206f 2013 702e fe127 6123 fb724 5213 ff221 f8321 fa1c0 1331 fd224 5610 7661 5620 7661 fa1a0 4727
  //   f9421 3115 2661 fd620 241 2661 fd610 fa1c0 f8271 fa110
endmodule
