// Logisim project Main_cook.circ as structural Verilog: 1 circuit, main circuit main
module main (
  input  in_1,
  input  in_2,
  output [7:0] out_3,
  output [7:0] out_4,
  output [7:0] out_5,
  output [7:0] out_6,
  output [7:0] t4
);

  wire clock_1_out, main_3_alusrc, main_3_beq, main_3_bneq, main_3_jump, main_3_memread, main_3_memtoreg,
       main_3_memwrite, main_3_regdst, main_3_regwrite, main_4_zero_flag, multiplexer_4_out;
  wire [2:0] main_3_aluop;
  wire [3:0] main_1_dst_reg, main_1_opcode, main_1_src_1, main_1_src_2, multiplexer_2_out;
  wire [7:0] adder_1_out, adder_2_out, main_1_addrss_imm, main_1_jmpaddr, main_1_pc_read, main_2_read_data_1,
       main_2_read_data_2, main_4_output, main_5_data_read, multiplexer_1_out, multiplexer_3_out,
       multiplexer_5_out, multiplexer_6_out, multiplexer_7_out;

  Clock clock_1 (.out(clock_1_out));
  Multiplexer #(.width(8), .enable("false")) multiplexer_1 (
    .in0({8{1'b0}}), .in1(multiplexer_6_out), .out(multiplexer_1_out), .sel(in_1));
  // Probe on multiplexer_6_out
  // Probe on main_1_pc_read
  Instruction_mem_main main_1 (
    .PC_Write(multiplexer_1_out), .Clock(clock_1_out), .Reset(in_2), .PC_Read(main_1_pc_read),
    .Opcode(main_1_opcode), .Src_1(main_1_src_1), .Src_2(main_1_src_2), .Dst_reg(main_1_dst_reg),
    .JmpAddr(main_1_jmpaddr), .Addrss_imm(main_1_addrss_imm));  // open: Shft_amnt
  Adder adder_1 (.a(main_1_pc_read), .b(8'h1), .out(adder_1_out));  // open: cin, cout
  // Probe on main_1_opcode
  // Probe on main_1_src_1
  // Probe on main_1_src_2
  // Probe on main_1_dst_reg
  // Probe on multiplexer_2_out
  Multiplexer #(.width(4), .enable("false")) multiplexer_2 (
    .in0(main_1_src_2), .in1(main_1_dst_reg), .out(multiplexer_2_out), .sel(main_3_regdst));
  Register_file_main main_2 (
    .Dst_Reg_1(multiplexer_2_out), .WriteData(multiplexer_7_out), .CLR(in_2), .SrcReg1(main_1_src_1),
    .SrcReg2(main_1_src_2), .RegWrite(main_3_regwrite), .CLK(clock_1_out),
    .t3__t2__t1__t0({out_6, out_5, out_4, out_3}), .t4(t4), .Read_Data_1(main_2_read_data_1),
    .Read_Data_2(main_2_read_data_2));
  Adder adder_2 (.a(main_1_addrss_imm), .b(adder_1_out), .out(adder_2_out));  // open: cin, cout
  Control_Unit_main main_3 (
    .OP_Code(main_1_opcode), .ALUOp(main_3_aluop), .Jump(main_3_jump), .bneq(main_3_bneq), .beq(main_3_beq),
    .MemWrite(main_3_memwrite), .MemRead(main_3_memread), .RegWrite(main_3_regwrite),
    .MemToReg(main_3_memtoreg), .ALUSrc(main_3_alusrc), .RegDst(main_3_regdst));
  // Probe on main_2_read_data_1
  Multiplexer #(.width(8), .enable("false")) multiplexer_3 (
    .in0(adder_1_out), .in1(adder_2_out), .out(multiplexer_3_out), .sel(multiplexer_4_out));
  Multiplexer #(.enable("false")) multiplexer_4 (
    .in0(main_3_bneq), .in1(main_3_beq), .out(multiplexer_4_out), .sel(main_4_zero_flag));
  // Probe on multiplexer_5_out
  Multiplexer #(.width(8), .enable("false")) multiplexer_5 (
    .in0(main_2_read_data_2), .in1(main_1_addrss_imm), .out(multiplexer_5_out), .sel(main_3_alusrc));
  New_alu_main main_4 (
    .ALUOp(main_3_aluop), .A(main_2_read_data_1), .B(multiplexer_5_out), .Output(main_4_output),
    .Zero_flag(main_4_zero_flag));
  // Probe on main_4_output
  // Probe on main_2_read_data_2
  Multiplexer #(.width(8), .enable("false")) multiplexer_6 (
    .in0(multiplexer_3_out), .in1(main_1_jmpaddr), .out(multiplexer_6_out), .sel(main_3_jump));
  Data_Memory_main main_5 (
    .Address(main_4_output), .Write_Data(main_2_read_data_2), .CLK(clock_1_out), .CLR(in_2),
    .Data_Read(main_5_data_read), .MemRead(main_3_memread), .MemWrite(main_3_memwrite));
  Multiplexer #(.width(8), .enable("false")) multiplexer_7 (
    .in0(main_4_output), .in1(main_5_data_read), .out(multiplexer_7_out), .sel(main_3_memtoreg));

  // Notes on the sheet:
  //   $t0
  //   $t1
  //   $t2
  //   $t3
endmodule
