// Logisim project Register_Implementation.circ as structural Verilog: 2 circuits, main circuit Memory_Cell
module Memory_Cell (
  input  D,
  input  CLK,
  input  Reset,
  output Output
);

  wire d_ff_1_q, not_1_out;

  not not_1 (not_1_out, CLK);
  D_Flip_Flop #(.trigger("high")) d_ff_1 (
    .clk(1'b1), .D(D), .Q(d_ff_1_q), .en(not_1_out), .reset(Reset));  // open: Qn, preset
  D_Flip_Flop #(.trigger("high")) d_ff_2 (
    .clk(1'b1), .D(d_ff_1_q), .Q(Output), .en(CLK), .reset(Reset));  // open: Qn, preset
endmodule

module Register (
  input  [7:0] Input,
  input  Reset,
  input  CLK,
  output [7:0] Stored_Data
);

  Memory_Cell _0 (.Output(Stored_Data[0]), .D(Input[0]), .CLK(CLK), .Reset(Reset));
  Memory_Cell _1 (.Output(Stored_Data[1]), .D(Input[1]), .CLK(CLK), .Reset(Reset));
  Memory_Cell _2 (.Output(Stored_Data[2]), .D(Input[2]), .CLK(CLK), .Reset(Reset));
  Memory_Cell _3 (.Output(Stored_Data[3]), .D(Input[3]), .CLK(CLK), .Reset(Reset));
  Memory_Cell _4 (.Output(Stored_Data[4]), .D(Input[4]), .CLK(CLK), .Reset(Reset));
  Memory_Cell _5 (.Output(Stored_Data[5]), .D(Input[5]), .CLK(CLK), .Reset(Reset));
  Memory_Cell _6 (.Output(Stored_Data[6]), .D(Input[6]), .CLK(CLK), .Reset(Reset));
  Memory_Cell _7 (.Output(Stored_Data[7]), .D(Input[7]), .CLK(CLK), .Reset(Reset));
endmodule
