// Logisim project Register_file.circ as structural Verilog: 1 circuit, main circuit main
module main (
  input  RegWrite,
  input  CLK,
  input  [3:0] Dst_Reg_1,
  input  [7:0] WriteData,
  input  CLR,
  input  [3:0] SrcReg1,
  input  [3:0] SrcReg2,
  output [31:0] t3__t2__t1__t0,
  output [7:0] t4,
  output [7:0] sp,
  output [7:0] Read_Data_1,
  output [7:0] Read_Data_2
);

  wire and_1_out, and_2_out, demultiplexer_1_out1, demultiplexer_1_out2, demultiplexer_1_out3,
       demultiplexer_1_out4, demultiplexer_1_out6, demultiplexer_1_out7, not_1_out, not_2_out, not_3_out,
       not_4_out, not_5_out, not_6_out, not_7_out;
  wire [7:0] multiplexer_3_out;

  not not_1 (not_1_out, demultiplexer_1_out1);
  Register t1 (.Input(WriteData), .Reset(CLR), .CLK(not_1_out), .Stored_Data(t3__t2__t1__t0[15:8]));
  not not_2 (not_2_out, demultiplexer_1_out2);
  Register t2 (.Input(WriteData), .Reset(CLR), .CLK(not_2_out), .Stored_Data(t3__t2__t1__t0[23:16]));
  Multiplexer #(.select(3), .width(8), .enable("false")) multiplexer_1 (
    .in0({8{1'b0}}), .in1(t3__t2__t1__t0[15:8]), .in2(t3__t2__t1__t0[23:16]), .in3(t3__t2__t1__t0[31:24]),
    .in4(t4), .in5({8{1'b0}}), .in6(sp), .in7(t3__t2__t1__t0[7:0]), .out(Read_Data_1), .sel(SrcReg1[2:0]));
  Demultiplexer #(.select(3), .enable("false")) demultiplexer_1 (
    .out1(demultiplexer_1_out1), .out2(demultiplexer_1_out2), .out3(demultiplexer_1_out3),
    .out4(demultiplexer_1_out4), .out6(demultiplexer_1_out6), .out7(demultiplexer_1_out7), .in(and_1_out),
    .sel(Dst_Reg_1[2:0]));  // open: out0, out5
  not not_3 (not_3_out, demultiplexer_1_out3);
  Register t3 (.Input(WriteData), .Reset(CLR), .CLK(not_3_out), .Stored_Data(t3__t2__t1__t0[31:24]));
  and and_1 (and_1_out, RegWrite, CLK);
  not not_4 (not_4_out, demultiplexer_1_out4);
  Register u_t4 (.Input(WriteData), .Reset(CLR), .CLK(not_4_out), .Stored_Data(t4));
  Multiplexer #(.select(3), .width(8), .enable("false")) multiplexer_2 (
    .in0({8{1'b0}}), .in1(t3__t2__t1__t0[15:8]), .in2(t3__t2__t1__t0[23:16]), .in3(t3__t2__t1__t0[31:24]),
    .in4(t4), .in5({8{1'b0}}), .in6(sp), .in7(t3__t2__t1__t0[7:0]), .out(Read_Data_2), .sel(SrcReg2[2:0]));
  not not_5 (not_5_out, demultiplexer_1_out7);
  Register t0 (.Input(WriteData), .Reset(CLR), .CLK(not_5_out), .Stored_Data(t3__t2__t1__t0[7:0]));
  not not_6 (not_6_out, demultiplexer_1_out6);
  Multiplexer #(.width(8), .enable("false")) multiplexer_3 (
    .in0(WriteData), .in1({8{1'b1}}), .out(multiplexer_3_out), .sel(CLR));
  not not_7 (not_7_out, CLR);
  and and_2 (and_2_out, not_6_out, not_7_out);
  Register u_sp (.Input(multiplexer_3_out), .Reset(1'b0), .CLK(and_2_out), .Stored_Data(sp));

  // Notes on the sheet:
  //   $zero
  //   $t3
  //   $t2
  //   $t1
  //   $t0
endmodule
